# Fritzing sketch SmartWatch_PCB_01 (saved by Fritzing 0.9.1b)
circuit board: 3cm x 1.8cm
circuit board: 2.4cm x 1.5cm
circuit board: 2.2cm x 1cm
circuit board: 2.95cm x 1.8cm
breadboards: 1

parts:
  Pad20 = Pad [width=2 height=0.9 connect=center]  # not connected
  Pad21 = Pad [width=2 height=0.9 connect=center]  # not connected
  Pad22 = Pad [width=2 height=0.9 connect=center]  # not connected
  Pad23 = Pad [width=2 height=0.9 connect=center]  # not connected
  Pad24 = Pad [width=2 height=0.9 connect=center]  # not connected
  Pad25 = Pad [width=2 height=0.9 connect=center]  # not connected
  Pad26 = Pad [width=2 height=0.9 connect=center]  # not connected
  Pad27 = Pad [width=2 height=0.9 connect=center]  # not connected
  Pad28 = Pad [width=2 height=0.9 connect=center]  # not connected
  Pad29 = Pad [width=2 height=0.9 connect=center]  # not connected
  Pad30 = Pad [width=2 height=0.9 connect=center]  # not connected
  Pad31 = Pad [width=2 height=0.9 connect=center]  # not connected
  Pad32 = Pad [width=2 height=0.9 connect=center]  # not connected
  Pad33 = Pad [width=2 height=0.9 connect=center]  # not connected
  Pad34 = Pad [width=2 height=0.9 connect=center]  # not connected
  Pad35 = Pad [width=2 height=0.9 connect=center]  # not connected
  S1 = Pushbutton [package=THT]  # not connected
  S3 = Pushbutton [package=THT]  # not connected
  S2 = Pushbutton [package=THT]  # not connected
  IC1 = LQFP-48 [chip_label=IC package=LQFP]
  Pad80 = Pad [width=3 height=0.5 connect=center]  # not connected
  Pad81 = Pad [width=3 height=0.5 connect=center]  # not connected
  Pad82 = Pad [width=3 height=0.5 connect=center]  # not connected
  Pad83 = Pad [width=3 height=0.5 connect=center]  # not connected
  Pad84 = Pad [width=3 height=0.5 connect=center]  # not connected
  Pad85 = Pad [width=3 height=0.5 connect=center]  # not connected
  Pad86 = Pad [width=3 height=0.5 connect=center]  # not connected
  Pad87 = Pad [width=3 height=0.5 connect=center]  # not connected
  Pad88 = Pad [width=3 height=0.5 connect=center]  # not connected
  Pad89 = Pad [width=3 height=0.5 connect=center]  # not connected
  Pad90 = Pad [width=3 height=0.5 connect=center]  # not connected
  Pad91 = Pad [width=3 height=0.5 connect=center]  # not connected
  Pad92 = Pad [width=3 height=0.5 connect=center]  # not connected
  Pad93 = Pad [width=3 height=0.5 connect=center]  # not connected
  Y3 = CRYSTAL [package=crystal-smd-5x3]
  C1 = Ceramic Capacitor [capacitance=100nF package="0603 [SMD, multilayer]"]
  C2 = Ceramic Capacitor [capacitance=100nF package="0603 [SMD, multilayer]"]
  C4 = Ceramic Capacitor [capacitance=100nF package="0603 [SMD, multilayer]"]
  C6 = Ceramic Capacitor [capacitance=100nF package="0603 [SMD, multilayer]"]
  C7 = Ceramic Capacitor [capacitance=100nF package="0603 [SMD, multilayer]"]
  Y4 = CRYSTAL [package=crystal-smd-5x3]
  C8 = Ceramic Capacitor [capacitance=100nF package="0603 [SMD, multilayer]"]  # not connected
  C9 = Ceramic Capacitor [capacitance=100nF package="0603 [SMD, multilayer]"]  # not connected
  C10 = Ceramic Capacitor [capacitance=100nF package="0603 [SMD, multilayer]"]  # not connected
  C11 = Ceramic Capacitor [capacitance=100nF package="0603 [SMD, multilayer]"]  # not connected
  Pad94 = Pad [width=2.3 height=0.9 connect=center]  # not connected
  Pad95 = Pad [width=2.3 height=0.9 connect=center]  # not connected
  Pad96 = Pad [width=2.3 height=0.9 connect=center]  # not connected
  Pad97 = Pad [width=2.3 height=0.9 connect=center]  # not connected
  Pad98 = Pad [width=2.3 height=0.9 connect=center]  # not connected
  Pad99 = Pad [width=2.3 height=0.9 connect=center]  # not connected
  Pad100 = Pad [width=2.3 height=0.9 connect=center]  # not connected
  Pad101 = Pad [width=2.3 height=0.9 connect=center]  # not connected
  Pad102 = Pad [width=2.3 height=0.9 connect=center]  # not connected
  Pad103 = Pad [width=2.3 height=0.9 connect=center]  # not connected
  Pad104 = Pad [width=2.3 height=0.9 connect=center]  # not connected
  Pad105 = Pad [width=2.3 height=0.9 connect=center]  # not connected
  Pad106 = Pad [width=2.3 height=0.9 connect=center]  # not connected
  Pad107 = Pad [width=2.3 height=0.9 connect=center]  # not connected
  Pad108 = Pad [width=2.3 height=0.9 connect=center]  # not connected
  Pad109 = Pad [width=2.3 height=0.9 connect=center]  # not connected
  Pad110 = Pad [width=2.3 height=0.9 connect=center]  # not connected
  Pad111 = Pad [width=2.3 height=0.9 connect=center]  # not connected
  Pad112 = Pad [width=2.3 height=0.9 connect=center]  # not connected
  Pad113 = Pad [width=2.3 height=0.9 connect=center]  # not connected
  Pad114 = Pad [width=2.3 height=0.9 connect=center]  # not connected
  Pad115 = Pad [width=2.3 height=0.9 connect=center]  # not connected
  Pad116 = Pad [width=2.3 height=0.9 connect=center]  # not connected
  Pad117 = Pad [width=2.3 height=0.9 connect=center]  # not connected
  Pad118 = Pad [width=2.3 height=0.9 connect=center]  # not connected
  Pad119 = Pad [width=2.3 height=0.9 connect=center]  # not connected
  U1 = ADXL345 [package=lga14]  # not connected
  C12 = Ceramic Capacitor [capacitance=100nF package="0603 [SMD, multilayer]"]  # not connected

nets:
  N1: IC1.1, C6.1
  N2: IC1.2, C6.0
  N3: IC1.13, C1.1
  N4: IC1.14, C1.0
  N5: IC1.23, C2.1
  N6: IC1.24, C2.0
  N7: IC1.43, Y4.1
  N8: IC1.44, Y4.2
  N9: IC1.45, Y3.1, C4.0
  N10: IC1.46, Y3.2, C7.1
