# Fritzing sketch SmartWatch_PCB_04 (saved by Fritzing 0.9.1b)
circuit board: 2.95cm x 1.8cm
breadboards: 1

parts:
  Pad20 = Pad [width=2 height=0.9 connect=center]  # not connected
  Pad21 = Pad [width=2 height=0.9 connect=center]  # not connected
  Pad22 = Pad [width=2 height=0.9 connect=center]  # not connected
  Pad23 = Pad [width=2 height=0.9 connect=center]
  Pad24 = Pad [width=2 height=0.9 connect=center]  # not connected
  Pad25 = Pad [width=2 height=0.9 connect=center]  # not connected
  Pad26 = Pad [width=2 height=0.9 connect=center]
  Pad27 = Pad [width=2 height=0.9 connect=center]  # not connected
  Pad28 = Pad [width=2 height=0.9 connect=center]  # not connected
  Pad29 = Pad [width=2 height=0.9 connect=center]  # not connected
  Pad30 = Pad [width=2 height=0.9 connect=center]  # not connected
  Pad31 = Pad [width=2 height=0.9 connect=center]  # not connected
  Pad32 = Pad [width=2 height=0.9 connect=center]  # not connected
  Pad33 = Pad [width=2 height=0.9 connect=center]  # not connected
  Pad34 = Pad [width=2 height=0.9 connect=center]  # not connected
  Pad35 = Pad [width=2 height=0.9 connect=center]  # not connected
  IC1 = LQFP-48 [chip_label=IC package=LQFP]
  Pad80 = Pad [width=3 height=0.5 connect=center]  # not connected
  Pad81 = Pad [width=3 height=0.5 connect=center]  # not connected
  Pad82 = Pad [width=3 height=0.5 connect=center]  # not connected
  Pad83 = Pad [width=3 height=0.5 connect=center]
  Pad84 = Pad [width=3 height=0.5 connect=center]  # not connected
  Pad85 = Pad [width=3 height=0.5 connect=center]  # not connected
  Pad86 = Pad [width=3 height=0.5 connect=center]
  Pad87 = Pad [width=3 height=0.5 connect=center]  # not connected
  Pad88 = Pad [width=3 height=0.5 connect=center]  # not connected
  Pad89 = Pad [width=3 height=0.5 connect=center]  # not connected
  Pad90 = Pad [width=3 height=0.5 connect=center]  # not connected
  Pad91 = Pad [width=3 height=0.5 connect=center]  # not connected
  Pad92 = Pad [width=3 height=0.5 connect=center]  # not connected
  Pad93 = Pad [width=3 height=0.5 connect=center]  # not connected
  C8 = Ceramic Capacitor [capacitance=100nF package="0603 [SMD, multilayer]"]  # not connected
  C9 = Ceramic Capacitor [capacitance=100nF package="0603 [SMD, multilayer]"]  # not connected
  C10 = Ceramic Capacitor [capacitance=100nF package="0603 [SMD, multilayer]"]  # not connected
  C11 = Ceramic Capacitor [capacitance=100nF package="0603 [SMD, multilayer]"]  # not connected
  U1 = ADXL345 [package=lga14]  # not connected
  C12 = Ceramic Capacitor [capacitance=100nF package="0603 [SMD, multilayer]"]  # not connected
  J1 = female pin header, 1 pin [form="♀ (female)"]  # not connected
  J3 = female pin header, 1 pin [form="♀ (female)"]  # not connected
  J4 = female pin header, 1 pin [form="♀ (female)"]  # not connected
  J5 = female pin header, 1 pin [form="♀ (female)"]  # not connected
  C13 = Ceramic Capacitor [capacitance=100nF package="0603 [SMD, multilayer]"]
  Pad97 = Pad [width=1.5 height=1.8 connect=center]
  Pad98 = Pad [width=1.5 height=1.8 connect=center]
  C14 = Ceramic Capacitor [capacitance=100nF package="0603 [SMD, multilayer]"]
  C15 = Ceramic Capacitor [capacitance=100nF package="0603 [SMD, multilayer]"]
  C16 = Ceramic Capacitor [capacitance=100nF package="0603 [SMD, multilayer]"]  # not connected
  C17 = Ceramic Capacitor [capacitance=100nF package="0603 [SMD, multilayer]"]  # not connected
  Pad99 = Pad [width=2 height=2.4 connect=center]  # not connected
  Pad100 = Pad [width=2 height=2.4 connect=center]  # not connected
  Pad105 = Pad [width=1.1 height=1.1 connect=center]
  Pad106 = Pad [width=1.1 height=1.1 connect=center]  # not connected
  Pad107 = Pad [width=1.1 height=1.1 connect=center]
  Pad108 = Pad [width=1.1 height=1.1 connect=center]
  C18 = Ceramic Capacitor [capacitance=100nF package="0603 [SMD, multilayer]"]  # not connected
  C19 = Ceramic Capacitor [capacitance=100nF package="0603 [SMD, multilayer]"]

nets:
  N1: Pad23.pad, IC1.18
  N2: Pad26.pad, IC1.19
  N3: IC1.1, C15.0
  N4: IC1.6, Pad107.pad
  N5: IC1.7, Pad108.pad
  N6: IC1.13, C13.0
  N7: IC1.25, C14.0
  N8: IC1.37, Pad105.pad
  N9: IC1.45, Pad98.pad
  N10: IC1.46, Pad97.pad, C19.1
  N11: Pad83.pad, Pad86.pad

notes:
  TX
  RX
  VC
  Rst
  GN
  KEY
  LED
  1
  14
  RS
  SDA
  GND
  -+
  SCK
  VCC
  CS
